# Fritzing sketch MiniDrivhus (saved by Fritzing 0.9.3b)
breadboards: 1

parts:
  Part1 = Arduino Uno (Rev3)
  Part2 = Soil Moisture Sensor
  R2 = Resistor [tolerance=±5% resistance=1k package=THT]
  Q1 = NPN-Transistor [package="TO92 [THT]"]
  RHT1 = Humidity and Temperature Sensor RHT03
  M1 = DC Motor
  Q2 = NPN-Transistor [package="TO92 [THT]"]
  Q3 = NPN-Transistor [package="TO92 [THT]"]
  R3 = Resistor [tolerance=±5% resistance=1k package=THT]
  R4 = Resistor [tolerance=±5% resistance=1k package=THT]
  Light_Sensor = mystery part, 3 pins [chip_label="Light Sensor"]

nets:
  N1: Part1.A0, Part2.SIG, Light_Sensor.pin3
  N2: Part1.GND, Q1.E, RHT1.GND_2, Q2.E, Q3.E
  N3: Part1.D2, RHT1.Data-signal
  N4: Part1.D4, R3.Pin_0
  N5: Part1.D5_PWM, R2.Pin_0
  N6: Part1.D6_PWM, R4.Pin_0
  3V3: Part1.3V3, Part2.VCC, Light_Sensor.pin2
  5V: Part1.5V, RHT1.Vcc, M1.pin_1
  N7: Part2.GND, Q3.C
  N8: R2.Pin_1, Q1.B
  N9: Q1.C, M1.pin_2
  N10: Q2.B, R3.Pin_1
  N11: Q2.C, Light_Sensor.pin1
  N12: Q3.B, R4.Pin_1
